// Logisim project cofre_decisao.circ as structural Verilog: 1 circuit, main circuit main
module main (
  input  C,
  input  S,
  input  T1,
  input  T0,
  output ABRIR,
  output ERRAR,
  output BLOQUEAR
);

  wire not_1_out, not_2_out;

  not not_1 (not_1_out, S);
  not not_2 (not_2_out, T1);
  and and_1 (ABRIR, C, S);
  and and_2 (ERRAR, C, not_1_out, not_2_out);
  and and_3 (BLOQUEAR, C, not_1_out, T1);

  // Notes on the sheet:
  //   T0 nao e usado (eliminado no Karnaugh)
  //   Cofre Digital - logica de decisao no estado D4 (Secao 7.1 da A1)
  //   C = tecla # | S = senha correta | T1 T0 = erros anteriores
  //   ABRIR = C.S
  //   ERRAR = C.S'.T1'
  //   BLOQUEAR = C.S'.T1
endmodule
